# Fritzing sketch pico-scetch (saved by Fritzing 1.0.1rc)
breadboards: 1

parts:
  A1 = Raspberry Pi Pico W
  R3 = Resistor [tolerance=±5% resistance=330 package="2512 [SMD]"]
  R4 = Resistor [tolerance=±5% resistance=330 package="2512 [SMD]"]
  R5 = Resistor [tolerance=±5% resistance=330 package="2512 [SMD]"]
  LED1 = RGB LED - (4 legs) [color="Red (633nm)" current=30mA package="5 mm [THT]"]
  S1 = Pushbutton [package="[THT]"]
  U1 = BATTERY-2 [package=battery-aaa]  # not connected
  U2 = BATTERY-2 [package=battery-aaa]  # not connected

nets:
  N1: A1.pin_3, A1.pin_8, A1.pin_13, A1.pin_18, A1.pin_23, A1.pin_28, A1.pin_33, A1.pin_38, S1.Pin_1, S1.Pin_2
  N2: A1.pin_16, R4.Pin_1
  N3: A1.pin_17, LED1.common_anode
  N4: A1.pin_19, R3.Pin_1
  N5: A1.pin_21, S1.Pin_3, S1.Pin_4
  N6: R3.Pin_0, LED1.red_cathode
  N7: R4.Pin_0, LED1.green_cathode
  N8: R5.Pin_0, LED1.blue_cathode

custom parts:
  Raspberry Pi Pico W: Raspberry Pi Pico W. Based around the RP2040 microcontroller the Pico W is a low cost microcontroller device bringing Raspberry Pi quality, cost, and easy of use to the microcontroller space. The areas marked KEEPOUT in pcb silkscreen should not have traces running through them to avoid shorts on a soldered in module!
